# Fritzing sketch breadboard (saved by Fritzing 0.9.10b)
breadboards: 1

parts:
  DHT1 = Humidity and Temperature Sensor DHT11
  U1 = ESP32S-HiLetgo [part_number=ESP32S-HiLetgo]
  JACK1 = 2.1mm Barrel Jack with Terminal Block
  F1 = Fan - 4 wire [package=THT]
  M1 = RioRand LM2596
  F2 = Fan - 4 wire [package=THT]

nets:
  N1: DHT1.Vcc, U1.3.3, M1.Pin_3
  N2: DHT1.Data-signal, U1.GPIO18
  GND: DHT1.GND_1, U1.GND, JACK1.NEG, F1.GND, M1.Pin_2, M1.Pin_4, F2.GND
  N3: U1.GPIO34, F1.PWM
  N4: U1.GPIO25, F1.Tach, F2.Tach
  N5: U1.GPIO12, F2.PWM
  N6: JACK1.POS, F1.Power, M1.Pin_1, F2.Power

notes:
  3v3 rail
  12v rail
  PWM output
  Tach Input
  Temp Input

custom parts:
  Humidity and Temperature Sensor DHT11: Digital relative humidity & temperature sensor DHT11
  ESP32S-HiLetgo: HiLetgo ESP-WROOM-32 ESP32 ESP-32S Development Board 2.4GHz Dual-Mode WiFi + Bluetooth Dual Cores Microcontroller The ESP32 integrated with Antenna switches, RF Balun, power amplifiers, low-noise amplifiers, filters, and management modules, and the entire solution occupies the least area of PCB. 2.4 GHz Wi-Fi plus Bluetooth dual-mode chip, with TSMC Ultra-low power consumption 40nm technology,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
  Fan - 4 wire: Fan, 4 wire with tach.
